# Fritzing sketch GNSS reciever4 (saved by Fritzing 0.9.3b)
breadboards: 1

parts:
  U1 = mosaicHAT
  Součástka1 = Arduino Uno (Rev3) - ICSP
  A1 = 4in spi lcd display
  S1 = Toggle Switch [package=THT]
  S2 = Round Pushbutton
  LLC1 = Logic Level Converter [package="Breakout board"]
  LLC2 = Logic Level Converter [package="Breakout board"]
  VCC1 = Battery block 9V
  VCC2 = Battery block 9V

nets:
  N1: U1.pin_41, Součástka1.5V, A1.Pin_1, LLC1.HV, LLC2.HV
  N2: U1.pin_42, Součástka1.GND, A1.Pin_2, S1.L1, S2.leg1, LLC1.L-GND, LLC1.H-GND, LLC2.L-GND, LLC2.H-GND, VCC1.-, VCC2.-
  N3: U1.pin_50, Součástka1.D7
  N4: U1.pin_51, Součástka1.D8
  N5: Součástka1.D11_PWM/MOSI, LLC2.HV1
  N6: Součástka1.D12/MISO, LLC1.HV3
  N7: Součástka1.D13/SCK, LLC1.HV4
  N8: Součástka1.D2, S2.leg0
  N9: Součástka1.D3_PWM, LLC2.HV2
  N10: Součástka1.D4, LLC2.HV4
  N11: Součástka1.D5_PWM, LLC2.HV3
  N12: Součástka1.3V3, LLC1.LV, LLC2.LV
  N13: Součástka1.VIN, S1.COM
  N14: S1.L2, VCC1.+, VCC2.+

notes:
  dávejte pozor na které straně je HV a LV u převodníku. LV má být u displeje a HV je u arduina

custom parts:
  mosaicHAT: mosaicHAT - Raspberry Pi compatible GPS/GNSS board
  4in spi lcd display: 4.0inch color screen with 320x480 resolution of 65K colors and rich display colors.
  Logic Level Converter: 5V to/from 3.3V logic level converter
